// Logisim project circuit1c.circ as structural Verilog: 1 circuit, main circuit main
module main (
  input  A,
  input  B,
  input  C,
  output result
);

  wire and_1_out, and_2_out, and_3_out, and_4_out, and_5_out, notA, notB, notC, or_1_out;

  not not_1 (notA, A);
  not not_2 (notB, B);
  not not_3 (notC, C);
  and and_1 (and_1_out, notA, notC);
  and and_2 (and_2_out, A, notB);
  and and_3 (and_3_out, A, B);
  and and_4 (and_4_out, and_2_out, notC);
  and and_5 (and_5_out, and_3_out, C);
  or or_1 (or_1_out, and_1_out, and_4_out);
  or or_2 (result, or_1_out, and_5_out);
endmodule
