// Logisim project my_adder.circ as structural Verilog: 2 circuits, main circuit main
module main (
  input  [15:0] A,
  input  sub,
  input  [15:0] B,
  output [15:0] result,
  output ovf
);

  wire B3, B4, B5, B6, B7, B8, B9, B10, B11, B12, B13, B14, B15, Cout3, Cout4, Cout5, Cout6, Cout7, Cout8,
       Cout9, Cout10, Cout11, Cout12, Cout13, Cout14, Cout15, onebit_4_cout, onebit_5_cout, onebit_9_cout,
       xor_1_out, xor_4_out, xor_6_out;

  xor xor_1 (xor_1_out, sub, B[0]);
  xor xor_2 (B8, B[8], sub);
  xor xor_3 (B12, B[12], sub);
  onebit onebit_1 (.A(A[4]), .Cin(Cout3), .B(B4), .Sum(result[4]), .Cout(Cout4));
  onebit onebit_2 (.A(A[8]), .Cin(Cout7), .B(B8), .Sum(result[8]), .Cout(Cout8));
  onebit onebit_3 (.A(A[12]), .Cin(Cout11), .B(B12), .Sum(result[12]), .Cout(Cout12));
  onebit onebit_4 (.A(A[0]), .Cin(sub), .B(xor_1_out), .Sum(result[0]), .Cout(onebit_4_cout));
  xor xor_4 (xor_4_out, sub, B[1]);
  xor xor_5 (B9, B[9], sub);
  onebit onebit_5 (.A(A[1]), .Cin(onebit_4_cout), .B(xor_4_out), .Sum(result[1]), .Cout(onebit_5_cout));
  xor xor_6 (xor_6_out, sub, B[2]);
  onebit onebit_6 (.A(A[5]), .Cin(Cout4), .B(B5), .Sum(result[5]), .Cout(Cout5));
  onebit onebit_7 (.A(A[9]), .Cin(Cout8), .B(B9), .Sum(result[9]), .Cout(Cout9));
  xor xor_7 (B13, B[13], sub);
  onebit onebit_8 (.A(A[13]), .Cin(Cout12), .B(B13), .Sum(result[13]), .Cout(Cout13));
  onebit onebit_9 (.A(A[2]), .Cin(onebit_5_cout), .B(xor_6_out), .Sum(result[2]), .Cout(onebit_9_cout));
  xor xor_8 (B3, sub, B[3]);
  xor xor_9 (B4, B[4], sub);
  xor xor_10 (B6, B[6], sub);
  xor xor_11 (B10, B[10], sub);
  xor xor_12 (B14, B[14], sub);
  xor xor_13 (B5, B[5], sub);
  onebit onebit_10 (.A(A[6]), .Cin(Cout5), .B(B6), .Sum(result[6]), .Cout(Cout6));
  onebit onebit_11 (.A(A[10]), .Cin(Cout9), .B(B10), .Sum(result[10]), .Cout(Cout10));
  onebit onebit_12 (.A(A[14]), .Cin(Cout13), .B(B14), .Sum(result[14]), .Cout(Cout14));
  onebit onebit_13 (.A(A[3]), .Cin(onebit_9_cout), .B(B3), .Sum(result[3]), .Cout(Cout3));
  xor xor_14 (B7, B[7], sub);
  onebit onebit_14 (.A(A[7]), .Cin(Cout6), .B(B7), .Sum(result[7]), .Cout(Cout7));
  xor xor_15 (B11, B[11], sub);
  xor xor_16 (ovf, Cout14, Cout15);
  onebit onebit_15 (.A(A[11]), .Cin(Cout10), .B(B11), .Sum(result[11]), .Cout(Cout11));
  xor xor_17 (B15, B[15], sub);
  onebit onebit_16 (.A(A[15]), .Cin(Cout14), .B(B15), .Sum(result[15]), .Cout(Cout15));

  // Other names for the same wires on the sheet: six = B[6]; seven = B[7]; nine = B[9]; ten = B[10]; eleven = B[11];
  //   twelve = B[12]; thirteen = B[13]; fourteen = B[14]; fifteen = B[15]; sum4 = result[4]; sum5 = result[5];
  //   sum6 = result[6]; sum7 = result[7]; sum8 = result[8]; sum9 = result[9]; sum10 = result[10]; sum11 = result[11];
  //   sum12 = result[12]; sum13 = result[13]; sum14 = result[14]; sum15 = result[15]
endmodule

module onebit (
  input  A,
  input  Cin,
  input  B,
  output Sum,
  output Cout
);

  wire and_1_out, and_2_out, xor_1_out;

  xor xor_1 (xor_1_out, A, B);
  and and_1 (and_1_out, A, B);
  and and_2 (and_2_out, xor_1_out, Cin);
  or or_1 (Cout, and_2_out, and_1_out);
  xor xor_2 (Sum, Cin, xor_1_out);
endmodule
