// Logisim project robot.circ as structural Verilog: 1 circuit, main circuit main
module main (
  input  [1:0] in_leftright,
  input  in_speed,
  output [1:0] out_position,
  output out_blocked
);

  wire clk, D0, D0_1, D0_2, D0_3, D0_4, D1, D1_1, D1_2, D1_3, D1_4, D1_5, D1_6, D1_7, D1_8, D1_9, D1_10,
       D1_11, D1_12, D2, D2_1, D2_2, D2_3, D2_4, D2_5, D2_6, D2_7, D2_8, D2_9, D2_10, D2_11, D2_12,
       not_1_out, not_2_out, not_3_out, not_4_out, not_5_out, not_6_out, not_7_out, not_8_out, not_9_out,
       not_10_out, not_11_out, not_12_out, not_13_out, not_14_out, not_15_out, not_16_out, not_17_out,
       not_18_out, not_19_out, not_20_out, not_21_out, not_22_out, not_23_out, not_24_out, not_25_out,
       not_26_out, not_27_out, not_28_out, not_29_out, not_30_out, not_31_out, not_32_out, not_33_out,
       not_34_out, not_35_out, not_36_out, not_37_out, not_38_out, not_39_out, not_40_out, not_41_out,
       not_42_out, not_43_out, not_44_out, not_45_out, not_46_out, not_47_out, not_48_out, not_49_out,
       not_50_out, not_51_out, not_52_out, not_53_out, not_54_out, not_55_out, not_56_out, not_57_out,
       not_58_out, not_59_out, not_60_out, not_61_out, not_62_out, not_63_out, not_64_out, not_65_out,
       not_66_out, not_67_out, not_68_out, not_69_out, not_70_out, not_71_out, not_72_out, not_73_out,
       not_74_out, not_75_out, not_76_out, not_77_out, not_78_out;

  Clock clock_1 (.out(clk));
  not not_1 (not_1_out, out_position[1]);
  not not_2 (not_2_out, out_position[0]);
  not not_3 (not_3_out, out_blocked);
  not not_4 (not_4_out, out_position[1]);
  not not_5 (not_5_out, out_blocked);
  not not_6 (not_6_out, in_speed);
  not not_7 (not_7_out, out_position[0]);
  not not_8 (not_8_out, out_blocked);
  not not_9 (not_9_out, in_leftright[0]);
  not not_10 (not_10_out, out_blocked);
  not not_11 (not_11_out, in_leftright[1]);
  not not_12 (not_12_out, in_leftright[0]);
  not not_13 (not_13_out, out_blocked);
  not not_14 (not_14_out, in_leftright[0]);
  not not_15 (not_15_out, in_leftright[1]);
  not not_16 (not_16_out, in_leftright[0]);
  not not_17 (not_17_out, in_leftright[0]);
  not not_18 (not_18_out, in_leftright[0]);
  not not_19 (not_19_out, in_leftright[1]);
  and and_1 (D2_1, not_1_out, not_2_out, not_3_out, in_leftright[1], not_17_out, in_speed);
  and and_2 (D2_3, not_4_out, out_position[0], not_5_out, in_leftright[1], not_18_out, not_6_out);
  and and_3 (D2_5, not_7_out, not_8_out, out_position[1], not_19_out, not_9_out);
  and and_4 (D2_7, out_position[0], not_10_out, out_position[1], not_11_out, not_12_out);
  and and_5 (D2_9, out_position[0], not_13_out, out_position[1], in_leftright[1], not_14_out);
  and and_6 (D2_11, out_position[0], out_blocked, out_position[1], not_15_out, not_16_out);
  D_Flip_Flop Q2 (.D(D2), .clk(clk), .Q(out_position[1]));  // open: Qn, preset, reset
  D_Flip_Flop Q1 (.D(D1), .clk(clk), .Q(out_position[0]));  // open: Qn, preset, reset
  D_Flip_Flop Q0 (.D(D0), .clk(clk), .Q(out_blocked));  // open: Qn, preset, reset
  not not_20 (not_20_out, out_position[1]);
  not not_21 (not_21_out, out_position[0]);
  not not_22 (not_22_out, out_position[1]);
  not not_23 (not_23_out, in_leftright[0]);
  not not_24 (not_24_out, out_blocked);
  not not_25 (not_25_out, in_leftright[0]);
  not not_26 (not_26_out, out_position[0]);
  not not_27 (not_27_out, out_blocked);
  not not_28 (not_28_out, in_leftright[0]);
  not not_29 (not_29_out, out_blocked);
  not not_30 (not_30_out, in_leftright[1]);
  not not_31 (not_31_out, in_speed);
  not not_32 (not_32_out, in_leftright[0]);
  not not_33 (not_33_out, in_leftright[1]);
  not not_34 (not_34_out, in_speed);
  or or_1 (D2, D2_1, D2_2, D2_3, D2_4, D2_5, D2_6, D2_7, D2_8, D2_9, D2_10, D2_11, D2_12);
  and and_7 (D2_2, not_20_out, not_21_out, out_blocked, in_leftright[1], not_23_out, in_speed);
  and and_8 (D2_4, not_22_out, out_position[0], not_24_out, in_leftright[1], not_25_out, in_speed);
  and and_9 (D2_6, not_26_out, not_27_out, out_position[1], in_leftright[1], not_28_out);
  and and_10 (D2_8, out_position[1], out_position[0], not_29_out, not_30_out, in_leftright[0], not_31_out);
  and and_11 (D2_10, out_position[0], out_blocked, out_position[1], in_leftright[1], not_32_out);
  and and_12 (D2_12, out_position[1], out_position[0], out_blocked, not_33_out, in_leftright[0], not_34_out);
  not not_35 (not_35_out, out_position[1]);
  not not_36 (not_36_out, out_position[0]);
  not not_37 (not_37_out, out_blocked);
  not not_38 (not_38_out, in_speed);
  not not_39 (not_39_out, out_position[1]);
  not not_40 (not_40_out, out_blocked);
  not not_41 (not_41_out, out_position[0]);
  not not_42 (not_42_out, out_blocked);
  not not_43 (not_43_out, in_speed);
  not not_44 (not_44_out, out_blocked);
  not not_45 (not_45_out, in_leftright[1]);
  not not_46 (not_46_out, out_blocked);
  not not_47 (not_47_out, in_leftright[1]);
  not not_48 (not_48_out, in_leftright[0]);
  not not_49 (not_49_out, in_leftright[0]);
  not not_50 (not_50_out, in_leftright[1]);
  not not_51 (not_51_out, in_leftright[0]);
  not not_52 (not_52_out, in_leftright[1]);
  not not_53 (not_53_out, in_leftright[0]);
  not not_54 (not_54_out, in_leftright[0]);
  and and_13 (D1_1, not_35_out, not_36_out, not_37_out, in_leftright[1], not_49_out, not_38_out);
  and and_14 (D1_3, not_39_out, out_position[0], not_40_out, not_50_out, not_51_out);
  and and_15 (D1_5, out_position[1], not_41_out, not_42_out, not_52_out, in_leftright[0], not_43_out);
  and and_16 (D1_7, out_position[1], out_position[0], not_44_out, not_45_out, not_53_out);
  and and_17 (D1_9, out_position[1], out_position[0], not_46_out, in_leftright[1], not_54_out);
  and and_18 (D1_11, out_position[1], out_position[0], out_blocked, not_47_out, not_48_out);
  not not_55 (not_55_out, out_position[1]);
  not not_56 (not_56_out, out_position[0]);
  not not_57 (not_57_out, in_speed);
  not not_58 (not_58_out, out_position[1]);
  not not_59 (not_59_out, out_blocked);
  not not_60 (not_60_out, out_position[0]);
  not not_61 (not_61_out, out_blocked);
  not not_62 (not_62_out, out_blocked);
  not not_63 (not_63_out, in_leftright[1]);
  not not_64 (not_64_out, in_leftright[0]);
  not not_65 (not_65_out, in_leftright[0]);
  not not_66 (not_66_out, in_leftright[0]);
  not not_67 (not_67_out, in_leftright[0]);
  not not_68 (not_68_out, in_leftright[1]);
  or or_2 (D1, D1_1, D1_2, D1_3, D1_4, D1_5, D1_6, D1_7, D1_8, D1_9, D1_10, D1_11, D1_12);
  and and_19 (D1_4, not_58_out, out_position[0], not_59_out, in_leftright[1], not_65_out, in_speed);
  and and_20 (D1_6, out_position[1], not_60_out, not_61_out, in_leftright[1], not_66_out);
  and and_21 (D1_8, out_position[1], out_position[0], not_62_out, not_63_out, in_leftright[0], in_speed);
  and and_22 (D1_10, out_position[1], out_position[0], out_blocked, in_leftright[1], not_67_out);
  and and_23 (D1_12, out_position[1], out_position[0], out_blocked, not_68_out, in_leftright[0], in_speed);
  and and_24 (D1_2, not_55_out, not_56_out, out_blocked, in_leftright[1], not_64_out, not_57_out);
  not not_69 (not_69_out, out_position[1]);
  not not_70 (not_70_out, out_position[0]);
  not not_71 (not_71_out, out_blocked);
  not not_72 (not_72_out, out_blocked);
  not not_73 (not_73_out, in_leftright[1]);
  not not_74 (not_74_out, in_leftright[0]);
  and and_25 (D0_1, not_69_out, not_70_out, not_71_out, not_73_out, in_leftright[0]);
  and and_26 (D0_3, out_position[1], out_position[0], not_72_out, in_leftright[1], not_74_out);
  or or_3 (D0, D0_1, D0_2, D0_3, D0_4);
  not not_75 (not_75_out, out_position[1]);
  not not_76 (not_76_out, out_position[0]);
  not not_77 (not_77_out, in_leftright[0]);
  not not_78 (not_78_out, in_leftright[1]);
  and and_27 (D0_2, not_75_out, not_76_out, out_blocked, not_78_out, in_leftright[0]);
  and and_28 (D0_4, out_position[1], out_position[0], out_blocked, in_leftright[1], not_77_out);

  // Other names for the same wires on the sheet: in_s = in_speed; Q1 = out_position[0]; Q2 = out_position[1];
  //   Q0 = out_blocked
endmodule
