// Logisim project circuit1a.circ as structural Verilog: 1 circuit, main circuit main
module main (
  input  A,
  input  B,
  input  C,
  output result
);

  wire and_1_out, and_2_out, and_3_out, not_1_out, xor_1_out, xor_2_out;

  and and_1 (and_1_out, B, C);
  not not_1 (not_1_out, C);
  xor xor_1 (xor_1_out, A, and_1_out);
  and and_2 (and_2_out, B, not_1_out);
  and and_3 (and_3_out, A, not_1_out);
  xor xor_2 (xor_2_out, xor_1_out, and_2_out);
  or or_1 (result, xor_2_out, and_3_out);
endmodule
