// Logisim project cpu.circ as structural Verilog: 9 circuits, main circuit main
module main (
  input  reset
);

  wire add, addi, beqz, beqz_and_zero, blt, blt_and_neg, clk, in2_0, in2_1, in_put, j, jal, jr,
       keyboard_1_avail, lw, memory_latch_1_oe_latched, memory_latch_1_we_latched, msb, multiplexer_1_out,
       no, not_1_out, not_2_out, not_4_out, out_put, pc_extend_plus_1, pc_mux0, R_eq0, shamt_choose, sl, sr,
       sub, sw, WE_choose, write_choose, xo;
  wire [2:0] ALU_in, multiplexer_4_out, multiplexer_8_out, undriven;
  wire [3:0] opcode;
  wire [7:0] key_out;
  wire [11:0] addy;
  wire [14:0] adder_add_4_result;
  wire [15:0] adder_out, addy_extend, alu_1_outputdata, extend, extend_plus_1,
       memory_latch_1_address_latched, memory_latch_1_data_in_latched, multiplexer_3_out, multiplexer_7_out,
       pc_add, pc_in, pc_plus_1, pc_retain, ram_1_dout, readout_1, readout_2, register16_1_q, writedata;

  // Probe on pc_in
  Clock clock_1 (.out(clk));
  // Probe on extend
  // Probe on addy_extend
  Decoder #(.select(4)) decoder_1 (
    .out0(add), .out1(sub), .out2(addi), .out3(no), .out4(xo), .out5(sl), .out6(sr), .out7(lw), .out8(sw),
    .out9(beqz), .out10(blt), .out11(j), .out12(jr), .out13(jal), .out14(in_put), .out15(out_put),
    .sel(opcode));  // open: en
  Multiplexer #(.enable("false")) multiplexer_1 (.in0(1'b1), .in1(1'b0), .out(multiplexer_1_out), .sel(WE_choose));
  or or_1 (write_choose, addi, lw);
  // Probe on write_choose
  not not_1 (not_1_out, clk);
  Multiplexer #(.width(16), .enable("false")) multiplexer_2 (
    .in0(16'h1), .in1(extend_plus_1), .out(pc_add), .sel(pc_extend_plus_1));
  Keyboard keyboard_1 (.clk(not_2_out), .re(in_put), .clr(reset), .avail(keyboard_1_avail), .data(key_out[6:0]));
  not not_2 (not_2_out, clk);
  assign addy_extend = {{4{1'b0}}, addy};  // Bit_Extender bit_extender_1
  Multiplexer #(.select(2), .width(16), .enable("false")) multiplexer_3 (
    .in0(writedata), .in1(pc_retain), .in2({{8{1'b0}}, key_out}), .out(multiplexer_3_out), .sel({in_put, jal}));  // open: in3
  Multiplexer #(.select(2), .width(3), .enable("false")) multiplexer_4 (
    .in0(addy[5:3]), .in1(addy[8:6]), .in2(3'b111), .in3(undriven), .out(multiplexer_4_out),
    .sel({jal, write_choose}));
  nor nor_1 (R_eq0, readout_1[0], readout_1[1], readout_1[2], readout_1[3], readout_1[4], readout_1[5], readout_1[6], readout_1[7], readout_1[8], readout_1[9], readout_1[10], readout_1[11], readout_1[12], readout_1[13], readout_1[14], readout_1[15]);
  adder_add adder_add_1 (.A(extend), .B(16'h1), .result(extend_plus_1));  // open: sub, ovf
  not not_3 (key_out[7], keyboard_1_avail);
  // Probe on multiplexer_4_out
  adder_add adder_add_2 (.A(register16_1_q), .B(pc_add), .result(adder_out));  // open: sub, ovf
  register16 register16_1 (.D(pc_in), .Reset(reset), .WE(1'b1), .clk(not_1_out), .Q(register16_1_q));
  // Probe on register16_1_q
  // Probe on pc_in
  Multiplexer #(.select(2), .width(16), .enable("false")) multiplexer_5 (
    .in0(adder_out), .in1(addy_extend), .in2(readout_1), .out(pc_in), .sel({jr, pc_mux0}));  // open: in3
  Multiplexer #(.width(16), .enable("false")) multiplexer_6 (
    .in0(adder_out), .in1(readout_1), .out(pc_retain), .sel(jr));
  // Probe on addy[5:0]
  // Probe on addy
  ROM #(.addrWidth(16), .dataWidth(16)) rom_1 (.addr(register16_1_q), .data({opcode, addy}));
  and and_1 (beqz_and_zero, R_eq0, beqz);
  assign extend = {{10{addy[5]}}, addy[5:0]};  // Bit_Extender bit_extender_2
  TTY #(.rows(13), .cols(80)) tty_1 (.data(readout_1[6:0]), .clk(clk), .we(out_put), .clr(reset));
  // Probe on readout_2
  // Probe on extend
  or or_2 (WE_choose, sw, beqz, blt, j, jr, out_put);
  // Probe on {in2_1, in2_0}
  or or_3 (in2_1, addi, sw, lw);
  or or_4 (pc_mux0, j, jal);
  // Probe on readout_1
  RegisterFile registerfile_1 (
    .clk(clk), .reset(reset), .writedata(multiplexer_3_out), .RegWriteEnable(multiplexer_1_out),
    .writeport(multiplexer_4_out), .readin1(addy[11:9]), .readin2(addy[8:6]), .readout1(readout_1),
    .readout2(readout_2));
  Multiplexer #(.select(2), .width(16), .enable("false")) multiplexer_7 (
    .in0(readout_2), .in1({16{1'b0}}), .in2(extend), .out(multiplexer_7_out), .sel({in2_1, in2_0}));  // open: in3
  // Probe on {opcode, addy}
  and and_2 (blt_and_neg, blt, msb);
  or or_5 (shamt_choose, sl, sr);
  // Probe on opcode
  adder_add adder_add_3 (.A(pc_retain), .B(16'h1), .result(pc_plus_1));  // open: sub, ovf
  or or_6 (ALU_in[2], xo, sr, sl);
  or or_7 (ALU_in[1], addi, no, sr);
  or or_8 (ALU_in[0], sub, no, sl);
  Multiplexer #(.width(3), .enable("false")) multiplexer_8 (
    .in0(3'b000), .in1(addy[2:0]), .out(multiplexer_8_out), .sel(shamt_choose));
  or or_9 (in2_0, no, sl, sr);
  adder_add adder_add_4 (.A(readout_1), .sub(1'b1), .B(readout_2), .result({msb, adder_add_4_result}));  // open: ovf
  not not_4 (not_4_out, clk);
  or or_10 (pc_extend_plus_1, blt_and_neg, beqz_and_zero);
  ALU alu_1 (
    .InputData1(readout_1), .InputData2(multiplexer_7_out), .OpType(ALU_in), .shamt(multiplexer_8_out),
    .OutputData(alu_1_outputdata));
  memory_latch memory_latch_1 (
    .address(alu_1_outputdata), .WE(sw), .clk(not_4_out), .data_in(readout_2),
    .address_latched(memory_latch_1_address_latched), .WE_latched(memory_latch_1_we_latched),
    .OE_latched(memory_latch_1_oe_latched), .data_in_latched(memory_latch_1_data_in_latched));
  RAM #(.addrWidth(16), .dataWidth(16), .trigger("high"), .databus("bibus")) ram_1 (
    .addr(memory_latch_1_address_latched), .we(memory_latch_1_we_latched), .oe(memory_latch_1_oe_latched),
    .din(memory_latch_1_data_in_latched), .dout(ram_1_dout));
  // Probe on alu_1_outputdata
  Multiplexer #(.width(16), .enable("false")) multiplexer_9 (
    .in0(alu_1_outputdata), .in1(ram_1_dout), .out(writedata), .sel(lw));
  // Probe on lw

  // Other names for the same wires on the sheet: immediate[5:0] = addy[5:0]; Shamt[2:0] = addy[2:0];
  //   Rd[2:0] = addy[5:3]; Rt[2:0] = addy[8:6]; Rs[2:0] = addy[11:9]; Q0 = ALU_in[0]; Q1 = ALU_in[1]; Q2 = ALU_in[2]

  // Notes on the sheet:
  //   contents of rom_1 (hex, n*v repeats v):
  //   204a e008 22a0 f400 e008 22a0 f400 e008 22a0 f400 903f 903f 219e 903f 219f 903f 207f 2144 a282 2198
  //   903f 2145
endmodule

module register16 (
  input  [15:0] D,
  input  Reset,
  input  WE,
  input  clk,
  output [15:0] Q
);

  wire WEclk;

  and and_1 (WEclk, WE, clk);
  D_Flip_Flop d_ff_1 (.D(D[0]), .clk(WEclk), .Q(Q[0]), .reset(Reset));  // open: Qn, preset
  D_Flip_Flop d_ff_2 (.D(D[4]), .clk(WEclk), .Q(Q[4]), .reset(Reset));  // open: Qn, preset
  D_Flip_Flop d_ff_3 (.D(D[8]), .clk(WEclk), .Q(Q[8]), .reset(Reset));  // open: Qn, preset
  D_Flip_Flop d_ff_4 (.D(D[12]), .clk(WEclk), .Q(Q[12]), .reset(Reset));  // open: Qn, preset
  D_Flip_Flop d_ff_5 (.D(D[1]), .clk(WEclk), .Q(Q[1]), .reset(Reset));  // open: Qn, preset
  D_Flip_Flop d_ff_6 (.D(D[5]), .clk(WEclk), .Q(Q[5]), .reset(Reset));  // open: Qn, preset
  D_Flip_Flop d_ff_7 (.D(D[9]), .clk(WEclk), .Q(Q[9]), .reset(Reset));  // open: Qn, preset
  D_Flip_Flop d_ff_8 (.D(D[13]), .clk(WEclk), .Q(Q[13]), .reset(Reset));  // open: Qn, preset
  D_Flip_Flop d_ff_9 (.D(D[2]), .clk(WEclk), .Q(Q[2]), .reset(Reset));  // open: Qn, preset
  D_Flip_Flop d_ff_10 (.D(D[6]), .clk(WEclk), .Q(Q[6]), .reset(Reset));  // open: Qn, preset
  D_Flip_Flop d_ff_11 (.D(D[10]), .clk(WEclk), .Q(Q[10]), .reset(Reset));  // open: Qn, preset
  D_Flip_Flop d_ff_12 (.D(D[14]), .clk(WEclk), .Q(Q[14]), .reset(Reset));  // open: Qn, preset
  D_Flip_Flop d_ff_13 (.D(D[3]), .clk(WEclk), .Q(Q[3]), .reset(Reset));  // open: Qn, preset
  D_Flip_Flop d_ff_14 (.D(D[7]), .clk(WEclk), .Q(Q[7]), .reset(Reset));  // open: Qn, preset
  D_Flip_Flop d_ff_15 (.D(D[11]), .clk(WEclk), .Q(Q[11]), .reset(Reset));  // open: Qn, preset
  D_Flip_Flop d_ff_16 (.D(D[15]), .clk(WEclk), .Q(Q[15]), .reset(Reset));  // open: Qn, preset

  // Other names for the same wires on the sheet: R = Reset
endmodule

module ALU (
  input  [15:0] InputData1,
  input  [15:0] InputData2,
  input  [2:0] OpType,
  input  [2:0] shamt,
  output [15:0] OutputData
);

  wire [15:0] result_add, result_NOT, result_sub, result_XOR, shift_left, shift_right;

  left_shift left_shift_1 (.data(InputData1), .shift(shamt), .result(shift_left));
  assign result_XOR = InputData1 ^ InputData2;  // XOR_Gate xor_1, 16 bits wide
  adder_add adder_add_1 (.A(InputData1), .sub(1'b0), .B(InputData2), .result(result_add));  // open: ovf
  adder_add adder_add_2 (.A(InputData1), .sub(1'b1), .B(InputData2), .result(result_sub));  // open: ovf
  assign result_NOT = ~InputData1;  // NOT_Gate not_1, 16 bits wide
  right_shift right_shift_1 (.data(InputData1), .shift(shamt), .result(shift_right));
  Multiplexer #(.select(3), .width(16), .enable("false")) multiplexer_1 (
    .in0(result_add), .in1(result_sub), .in2(result_add), .in3(result_NOT), .in4(result_XOR),
    .in5(shift_left), .in6(shift_right), .out(OutputData), .sel(OpType));  // open: in7

  // Other names for the same wires on the sheet: in1[15:0] = InputData1; in2[15:0] = InputData2; op[2:0] = OpType;
  //   shift[2:0] = shamt
endmodule

module adder_add (
  input  [15:0] A,
  input  sub,
  input  [15:0] B,
  output [15:0] result,
  output ovf
);

  wire B3, B4, B5, B6, B7, B8, B9, B10, B11, B12, B13, B14, B15, Cout3, Cout4, Cout5, Cout6, Cout7, Cout8,
       Cout9, Cout10, Cout11, Cout12, Cout13, Cout14, Cout15, onebit_4_cout, onebit_5_cout, onebit_9_cout,
       xor_1_out, xor_4_out, xor_6_out;

  xor xor_1 (xor_1_out, sub, B[0]);
  xor xor_2 (B8, B[8], sub);
  xor xor_3 (B12, B[12], sub);
  onebit onebit_1 (.A(A[4]), .Cin(Cout3), .B(B4), .Sum(result[4]), .Cout(Cout4));
  onebit onebit_2 (.A(A[8]), .Cin(Cout7), .B(B8), .Sum(result[8]), .Cout(Cout8));
  onebit onebit_3 (.A(A[12]), .Cin(Cout11), .B(B12), .Sum(result[12]), .Cout(Cout12));
  onebit onebit_4 (.A(A[0]), .Cin(sub), .B(xor_1_out), .Sum(result[0]), .Cout(onebit_4_cout));
  xor xor_4 (xor_4_out, sub, B[1]);
  xor xor_5 (B9, B[9], sub);
  onebit onebit_5 (.A(A[1]), .Cin(onebit_4_cout), .B(xor_4_out), .Sum(result[1]), .Cout(onebit_5_cout));
  xor xor_6 (xor_6_out, sub, B[2]);
  onebit onebit_6 (.A(A[5]), .Cin(Cout4), .B(B5), .Sum(result[5]), .Cout(Cout5));
  onebit onebit_7 (.A(A[9]), .Cin(Cout8), .B(B9), .Sum(result[9]), .Cout(Cout9));
  xor xor_7 (B13, B[13], sub);
  onebit onebit_8 (.A(A[13]), .Cin(Cout12), .B(B13), .Sum(result[13]), .Cout(Cout13));
  onebit onebit_9 (.A(A[2]), .Cin(onebit_5_cout), .B(xor_6_out), .Sum(result[2]), .Cout(onebit_9_cout));
  xor xor_8 (B3, sub, B[3]);
  xor xor_9 (B4, B[4], sub);
  xor xor_10 (B6, B[6], sub);
  xor xor_11 (B10, B[10], sub);
  xor xor_12 (B14, B[14], sub);
  xor xor_13 (B5, B[5], sub);
  onebit onebit_10 (.A(A[6]), .Cin(Cout5), .B(B6), .Sum(result[6]), .Cout(Cout6));
  onebit onebit_11 (.A(A[10]), .Cin(Cout9), .B(B10), .Sum(result[10]), .Cout(Cout10));
  onebit onebit_12 (.A(A[14]), .Cin(Cout13), .B(B14), .Sum(result[14]), .Cout(Cout14));
  onebit onebit_13 (.A(A[3]), .Cin(onebit_9_cout), .B(B3), .Sum(result[3]), .Cout(Cout3));
  xor xor_14 (B7, B[7], sub);
  onebit onebit_14 (.A(A[7]), .Cin(Cout6), .B(B7), .Sum(result[7]), .Cout(Cout7));
  xor xor_15 (B11, B[11], sub);
  xor xor_16 (ovf, Cout14, Cout15);
  onebit onebit_15 (.A(A[11]), .Cin(Cout10), .B(B11), .Sum(result[11]), .Cout(Cout11));
  xor xor_17 (B15, B[15], sub);
  onebit onebit_16 (.A(A[15]), .Cin(Cout14), .B(B15), .Sum(result[15]), .Cout(Cout15));

  // Other names for the same wires on the sheet: six = B[6]; seven = B[7]; nine = B[9]; ten = B[10]; eleven = B[11];
  //   twelve = B[12]; thirteen = B[13]; fourteen = B[14]; fifteen = B[15]; sum4 = result[4]; sum5 = result[5];
  //   sum6 = result[6]; sum7 = result[7]; sum8 = result[8]; sum9 = result[9]; sum10 = result[10]; sum11 = result[11];
  //   sum12 = result[12]; sum13 = result[13]; sum14 = result[14]; sum15 = result[15]
endmodule

module onebit (
  input  A,
  input  Cin,
  input  B,
  output Sum,
  output Cout
);

  wire and_1_out, and_2_out, xor_1_out;

  xor xor_1 (xor_1_out, A, B);
  and and_1 (and_1_out, A, B);
  and and_2 (and_2_out, xor_1_out, Cin);
  or or_1 (Cout, and_2_out, and_1_out);
  xor xor_2 (Sum, Cin, xor_1_out);
endmodule

module RegisterFile (
  input  clk,
  input  reset,
  input  [15:0] writedata,
  input  RegWriteEnable,
  input  [2:0] writeport,
  input  [2:0] readin1,
  input  [2:0] readin2,
  output [15:0] readout1,
  output [15:0] readout2
);

  wire readin11, readin12, readin13, readin14, readin15, readin16, readin17, readin18, readin21, readin22,
       readin23, readin24, readin25, readin26, readin27, readin28, WE1, WE2, WE3, WE4, WE5, WE6, WE7, WE8;
  wire [15:0] register16_1_q, register16_2_q, register16_3_q, register16_4_q, register16_5_q, register16_6_q,
       register16_7_q, register16_8_q;

  register16 register16_1 (.D({16{1'b0}}), .Reset(reset), .WE(WE1), .clk(clk), .Q(register16_1_q));
  register16 register16_2 (.D(writedata), .Reset(reset), .WE(WE2), .clk(clk), .Q(register16_2_q));
  register16 register16_3 (.D(writedata), .Reset(reset), .WE(WE3), .clk(clk), .Q(register16_3_q));
  register16 register16_4 (.D(writedata), .Reset(reset), .WE(WE4), .clk(clk), .Q(register16_4_q));
  register16 register16_5 (.D(writedata), .Reset(reset), .WE(WE5), .clk(clk), .Q(register16_5_q));
  register16 register16_6 (.D(writedata), .Reset(reset), .WE(WE6), .clk(clk), .Q(register16_6_q));
  register16 register16_7 (.D(writedata), .Reset(reset), .WE(WE8), .clk(clk), .Q(register16_7_q));
  Decoder #(.select(3)) decoder_1 (
    .out0(WE1), .out1(WE2), .out2(WE3), .out3(WE4), .out4(WE5), .out5(WE6), .out6(WE7), .out7(WE8),
    .sel(writeport), .en(RegWriteEnable));
  Decoder #(.select(3)) decoder_2 (
    .out0(readin11), .out1(readin12), .out2(readin13), .out3(readin14), .out4(readin15), .out5(readin16),
    .out6(readin17), .out7(readin18), .sel(readin1));  // open: en
  Decoder #(.select(3)) decoder_3 (
    .out0(readin21), .out1(readin22), .out2(readin23), .out3(readin24), .out4(readin25), .out5(readin26),
    .out6(readin27), .out7(readin28), .sel(readin2));  // open: en
  // Probe on register16_1_q
  // Probe on register16_2_q
  // Probe on register16_3_q
  // Probe on register16_4_q
  // Probe on register16_5_q
  // Probe on register16_6_q
  // Probe on register16_8_q
  register16 register16_8 (.D(writedata), .Reset(reset), .WE(WE7), .clk(clk), .Q(register16_8_q));
  // Probe on register16_7_q
  assign readout1 = readin11 ? register16_1_q : 16'bz;  // Controlled_Buffer controlled_buffer_1
  assign readout1 = readin12 ? register16_2_q : 16'bz;  // Controlled_Buffer controlled_buffer_2
  assign readout1 = readin13 ? register16_3_q : 16'bz;  // Controlled_Buffer controlled_buffer_3
  assign readout1 = readin14 ? register16_4_q : 16'bz;  // Controlled_Buffer controlled_buffer_4
  assign readout1 = readin15 ? register16_5_q : 16'bz;  // Controlled_Buffer controlled_buffer_5
  assign readout1 = readin16 ? register16_6_q : 16'bz;  // Controlled_Buffer controlled_buffer_6
  assign readout1 = readin17 ? register16_8_q : 16'bz;  // Controlled_Buffer controlled_buffer_7
  assign readout1 = readin18 ? register16_7_q : 16'bz;  // Controlled_Buffer controlled_buffer_8
  assign readout2 = readin21 ? register16_1_q : 16'bz;  // Controlled_Buffer controlled_buffer_9
  assign readout2 = readin22 ? register16_2_q : 16'bz;  // Controlled_Buffer controlled_buffer_10
  assign readout2 = readin23 ? register16_3_q : 16'bz;  // Controlled_Buffer controlled_buffer_11
  assign readout2 = readin24 ? register16_4_q : 16'bz;  // Controlled_Buffer controlled_buffer_12
  assign readout2 = readin25 ? register16_5_q : 16'bz;  // Controlled_Buffer controlled_buffer_13
  assign readout2 = readin26 ? register16_6_q : 16'bz;  // Controlled_Buffer controlled_buffer_14
  assign readout2 = readin27 ? register16_8_q : 16'bz;  // Controlled_Buffer controlled_buffer_15
  assign readout2 = readin28 ? register16_7_q : 16'bz;  // Controlled_Buffer controlled_buffer_16

  // Other names for the same wires on the sheet: weCLK = clk
endmodule

module memory_latch (
  input  [15:0] address,
  input  WE,
  input  clk,
  input  [15:0] data_in,
  output [15:0] address_latched,
  output WE_latched,
  output OE_latched,
  output [15:0] data_in_latched
);

  wire DMwe_latch_q;
  wire [15:0] addr_latch_q;

  Register #(.width(16), .trigger("falling")) addr_latch (
    .D(address), .en(WE), .clk(clk), .Q(addr_latch_q));  // open: clr
  D_Flip_Flop #(.trigger("falling")) DMwe_latch (.D(WE), .clk(clk), .Q(DMwe_latch_q));  // open: Qn, preset, reset
  Register #(.width(16), .trigger("falling")) data_to_be_written (
    .D(data_in), .en(WE), .clk(clk), .Q(data_in_latched));  // open: clr
  Multiplexer #(.width(16), .enable("false")) multiplexer_1 (
    .in0(address), .in1(addr_latch_q), .out(address_latched), .sel(DMwe_latch_q));
  and and_1 (WE_latched, clk, DMwe_latch_q);
  not not_1 (OE_latched, WE_latched);
endmodule

module left_shift (
  input  [15:0] data,
  input  [2:0] shift,
  output [15:0] result
);

  wire eight, el, fift, five, four, fourt, multiplexer_1_out, multiplexer_2_out, multiplexer_3_out,
       multiplexer_4_out, multiplexer_5_out, multiplexer_6_out, multiplexer_7_out, multiplexer_8_out,
       multiplexer_9_out, multiplexer_10_out, multiplexer_11_out, multiplexer_12_out, multiplexer_13_out,
       multiplexer_14_out, multiplexer_15_out, multiplexer_16_out, nine, one, seven, six, ten, thirt, three,
       twelf, two, zero;

  Multiplexer #(.enable("false")) multiplexer_1 (
    .in0(data[15]), .in1(data[14]), .out(multiplexer_1_out), .sel(shift[0]));
  Multiplexer #(.enable("false")) multiplexer_2 (
    .in0(data[14]), .in1(data[13]), .out(multiplexer_2_out), .sel(shift[0]));
  Multiplexer #(.enable("false")) multiplexer_3 (
    .in0(data[13]), .in1(data[12]), .out(multiplexer_3_out), .sel(shift[0]));
  Multiplexer #(.enable("false")) multiplexer_4 (
    .in0(data[12]), .in1(data[11]), .out(multiplexer_4_out), .sel(shift[0]));
  Multiplexer #(.enable("false")) multiplexer_5 (
    .in0(data[11]), .in1(data[10]), .out(multiplexer_5_out), .sel(shift[0]));
  Multiplexer #(.enable("false")) multiplexer_6 (
    .in0(data[10]), .in1(data[9]), .out(multiplexer_6_out), .sel(shift[0]));
  Multiplexer #(.enable("false")) multiplexer_7 (.in0(data[9]), .in1(data[8]), .out(multiplexer_7_out), .sel(shift[0]));
  Multiplexer #(.enable("false")) multiplexer_8 (.in0(data[8]), .in1(data[7]), .out(multiplexer_8_out), .sel(shift[0]));
  Multiplexer #(.enable("false")) multiplexer_9 (.in0(data[7]), .in1(data[6]), .out(multiplexer_9_out), .sel(shift[0]));
  Multiplexer #(.enable("false")) multiplexer_10 (
    .in0(data[6]), .in1(data[5]), .out(multiplexer_10_out), .sel(shift[0]));
  Multiplexer #(.enable("false")) multiplexer_11 (
    .in0(data[5]), .in1(data[4]), .out(multiplexer_11_out), .sel(shift[0]));
  Multiplexer #(.enable("false")) multiplexer_12 (
    .in0(data[4]), .in1(data[3]), .out(multiplexer_12_out), .sel(shift[0]));
  Multiplexer #(.enable("false")) multiplexer_13 (
    .in0(data[3]), .in1(data[2]), .out(multiplexer_13_out), .sel(shift[0]));
  Multiplexer #(.enable("false")) multiplexer_14 (
    .in0(data[2]), .in1(data[1]), .out(multiplexer_14_out), .sel(shift[0]));
  Multiplexer #(.enable("false")) multiplexer_15 (
    .in0(data[1]), .in1(data[0]), .out(multiplexer_15_out), .sel(shift[0]));
  Multiplexer #(.enable("false")) multiplexer_16 (.in0(data[0]), .in1(1'b0), .out(multiplexer_16_out), .sel(shift[0]));
  Multiplexer #(.enable("false")) multiplexer_17 (
    .in0(multiplexer_1_out), .in1(multiplexer_3_out), .out(fift), .sel(shift[1]));
  Multiplexer #(.enable("false")) multiplexer_18 (
    .in0(multiplexer_2_out), .in1(multiplexer_4_out), .out(fourt), .sel(shift[1]));
  Multiplexer #(.enable("false")) multiplexer_19 (
    .in0(multiplexer_3_out), .in1(multiplexer_5_out), .out(thirt), .sel(shift[1]));
  Multiplexer #(.enable("false")) multiplexer_20 (
    .in0(multiplexer_4_out), .in1(multiplexer_6_out), .out(twelf), .sel(shift[1]));
  Multiplexer #(.enable("false")) multiplexer_21 (
    .in0(multiplexer_5_out), .in1(multiplexer_7_out), .out(el), .sel(shift[1]));
  Multiplexer #(.enable("false")) multiplexer_22 (
    .in0(multiplexer_6_out), .in1(multiplexer_8_out), .out(ten), .sel(shift[1]));
  Multiplexer #(.enable("false")) multiplexer_23 (
    .in0(multiplexer_7_out), .in1(multiplexer_9_out), .out(nine), .sel(shift[1]));
  Multiplexer #(.enable("false")) multiplexer_24 (
    .in0(multiplexer_8_out), .in1(multiplexer_10_out), .out(eight), .sel(shift[1]));
  Multiplexer #(.enable("false")) multiplexer_25 (
    .in0(multiplexer_9_out), .in1(multiplexer_11_out), .out(seven), .sel(shift[1]));
  Multiplexer #(.enable("false")) multiplexer_26 (
    .in0(multiplexer_10_out), .in1(multiplexer_12_out), .out(six), .sel(shift[1]));
  Multiplexer #(.enable("false")) multiplexer_27 (
    .in0(multiplexer_11_out), .in1(multiplexer_13_out), .out(five), .sel(shift[1]));
  Multiplexer #(.enable("false")) multiplexer_28 (
    .in0(multiplexer_12_out), .in1(multiplexer_14_out), .out(four), .sel(shift[1]));
  Multiplexer #(.enable("false")) multiplexer_29 (
    .in0(multiplexer_13_out), .in1(multiplexer_15_out), .out(three), .sel(shift[1]));
  Multiplexer #(.enable("false")) multiplexer_30 (
    .in0(multiplexer_14_out), .in1(multiplexer_16_out), .out(two), .sel(shift[1]));
  Multiplexer #(.enable("false")) multiplexer_31 (.in0(multiplexer_15_out), .in1(1'b0), .out(one), .sel(shift[1]));
  Multiplexer #(.enable("false")) multiplexer_32 (.in0(multiplexer_16_out), .in1(1'b0), .out(zero), .sel(shift[1]));
  Multiplexer #(.enable("false")) multiplexer_33 (.in0(fift), .in1(el), .out(result[15]), .sel(shift[2]));
  Multiplexer #(.enable("false")) multiplexer_34 (.in0(fourt), .in1(ten), .out(result[14]), .sel(shift[2]));
  Multiplexer #(.enable("false")) multiplexer_35 (.in0(thirt), .in1(nine), .out(result[13]), .sel(shift[2]));
  Multiplexer #(.enable("false")) multiplexer_36 (.in0(twelf), .in1(eight), .out(result[12]), .sel(shift[2]));
  Multiplexer #(.enable("false")) multiplexer_37 (.in0(el), .in1(seven), .out(result[11]), .sel(shift[2]));
  Multiplexer #(.enable("false")) multiplexer_38 (.in0(ten), .in1(six), .out(result[10]), .sel(shift[2]));
  Multiplexer #(.enable("false")) multiplexer_39 (.in0(nine), .in1(five), .out(result[9]), .sel(shift[2]));
  Multiplexer #(.enable("false")) multiplexer_40 (.in0(eight), .in1(four), .out(result[8]), .sel(shift[2]));
  Multiplexer #(.enable("false")) multiplexer_41 (.in0(seven), .in1(three), .out(result[7]), .sel(shift[2]));
  Multiplexer #(.enable("false")) multiplexer_42 (.in0(six), .in1(two), .out(result[6]), .sel(shift[2]));
  Multiplexer #(.enable("false")) multiplexer_43 (.in0(five), .in1(one), .out(result[5]), .sel(shift[2]));
  Multiplexer #(.enable("false")) multiplexer_44 (.in0(four), .in1(zero), .out(result[4]), .sel(shift[2]));
  Multiplexer #(.enable("false")) multiplexer_45 (.in0(three), .in1(1'b0), .out(result[3]), .sel(shift[2]));
  Multiplexer #(.enable("false")) multiplexer_46 (.in0(two), .in1(1'b0), .out(result[2]), .sel(shift[2]));
  Multiplexer #(.enable("false")) multiplexer_47 (.in0(one), .in1(1'b0), .out(result[1]), .sel(shift[2]));
  Multiplexer #(.enable("false")) multiplexer_48 (.in0(zero), .in1(1'b0), .out(result[0]), .sel(shift[2]));

  // Other names for the same wires on the sheet: out0 = result[0]; out1 = result[1]; out2 = result[2];
  //   out3 = result[3]; out4 = result[4]; out5 = result[5]; out6 = result[6]; out7 = result[7]; out8 = result[8];
  //   out9 = result[9]; out10 = result[10]; out11 = result[11]; out12 = result[12]; out13 = result[13];
  //   out14 = result[14]; out15 = result[15]

  // Notes on the sheet:
  //   15
  //   14
  //   10
  //   9
  //   8
  //   7
  //   4
  //   2
  //   1
  //   0
  //   13
  //   12
  //   11
  //   6
  //   5
  //   3
endmodule

module right_shift (
  input  [15:0] data,
  input  [2:0] shift,
  output [15:0] result
);

  wire eight, el, fift, five, four, fourt, multiplexer_1_out, multiplexer_2_out, multiplexer_3_out,
       multiplexer_4_out, multiplexer_5_out, multiplexer_6_out, multiplexer_7_out, multiplexer_8_out,
       multiplexer_9_out, multiplexer_10_out, multiplexer_11_out, multiplexer_12_out, multiplexer_13_out,
       multiplexer_14_out, multiplexer_15_out, multiplexer_16_out, nine, one, seven, six, ten, thirt, three,
       twelf, two, zero;

  Multiplexer #(.enable("false")) multiplexer_1 (.in0(data[0]), .in1(data[1]), .out(multiplexer_1_out), .sel(shift[0]));
  Multiplexer #(.enable("false")) multiplexer_2 (.in0(data[1]), .in1(data[2]), .out(multiplexer_2_out), .sel(shift[0]));
  Multiplexer #(.enable("false")) multiplexer_3 (.in0(data[2]), .in1(data[3]), .out(multiplexer_3_out), .sel(shift[0]));
  Multiplexer #(.enable("false")) multiplexer_4 (.in0(data[3]), .in1(data[4]), .out(multiplexer_4_out), .sel(shift[0]));
  Multiplexer #(.enable("false")) multiplexer_5 (.in0(data[4]), .in1(data[5]), .out(multiplexer_5_out), .sel(shift[0]));
  Multiplexer #(.enable("false")) multiplexer_6 (.in0(data[5]), .in1(data[6]), .out(multiplexer_6_out), .sel(shift[0]));
  Multiplexer #(.enable("false")) multiplexer_7 (.in0(data[6]), .in1(data[7]), .out(multiplexer_7_out), .sel(shift[0]));
  Multiplexer #(.enable("false")) multiplexer_8 (.in0(data[7]), .in1(data[8]), .out(multiplexer_8_out), .sel(shift[0]));
  Multiplexer #(.enable("false")) multiplexer_9 (.in0(data[8]), .in1(data[9]), .out(multiplexer_9_out), .sel(shift[0]));
  Multiplexer #(.enable("false")) multiplexer_10 (
    .in0(data[9]), .in1(data[10]), .out(multiplexer_10_out), .sel(shift[0]));
  Multiplexer #(.enable("false")) multiplexer_11 (
    .in0(data[10]), .in1(data[11]), .out(multiplexer_11_out), .sel(shift[0]));
  Multiplexer #(.enable("false")) multiplexer_12 (
    .in0(data[11]), .in1(data[12]), .out(multiplexer_12_out), .sel(shift[0]));
  Multiplexer #(.enable("false")) multiplexer_13 (
    .in0(data[12]), .in1(data[13]), .out(multiplexer_13_out), .sel(shift[0]));
  Multiplexer #(.enable("false")) multiplexer_14 (
    .in0(data[13]), .in1(data[14]), .out(multiplexer_14_out), .sel(shift[0]));
  Multiplexer #(.enable("false")) multiplexer_15 (
    .in0(data[14]), .in1(data[15]), .out(multiplexer_15_out), .sel(shift[0]));
  Multiplexer #(.enable("false")) multiplexer_16 (.in0(data[15]), .in1(1'b0), .out(multiplexer_16_out), .sel(shift[0]));
  Multiplexer #(.enable("false")) multiplexer_17 (
    .in0(multiplexer_1_out), .in1(multiplexer_3_out), .out(fift), .sel(shift[1]));
  Multiplexer #(.enable("false")) multiplexer_18 (
    .in0(multiplexer_2_out), .in1(multiplexer_4_out), .out(fourt), .sel(shift[1]));
  Multiplexer #(.enable("false")) multiplexer_19 (
    .in0(multiplexer_3_out), .in1(multiplexer_5_out), .out(thirt), .sel(shift[1]));
  Multiplexer #(.enable("false")) multiplexer_20 (
    .in0(multiplexer_4_out), .in1(multiplexer_6_out), .out(twelf), .sel(shift[1]));
  Multiplexer #(.enable("false")) multiplexer_21 (
    .in0(multiplexer_5_out), .in1(multiplexer_7_out), .out(el), .sel(shift[1]));
  Multiplexer #(.enable("false")) multiplexer_22 (
    .in0(multiplexer_6_out), .in1(multiplexer_8_out), .out(ten), .sel(shift[1]));
  Multiplexer #(.enable("false")) multiplexer_23 (
    .in0(multiplexer_7_out), .in1(multiplexer_9_out), .out(nine), .sel(shift[1]));
  Multiplexer #(.enable("false")) multiplexer_24 (
    .in0(multiplexer_8_out), .in1(multiplexer_10_out), .out(eight), .sel(shift[1]));
  Multiplexer #(.enable("false")) multiplexer_25 (
    .in0(multiplexer_9_out), .in1(multiplexer_11_out), .out(seven), .sel(shift[1]));
  Multiplexer #(.enable("false")) multiplexer_26 (
    .in0(multiplexer_10_out), .in1(multiplexer_12_out), .out(six), .sel(shift[1]));
  Multiplexer #(.enable("false")) multiplexer_27 (
    .in0(multiplexer_11_out), .in1(multiplexer_13_out), .out(five), .sel(shift[1]));
  Multiplexer #(.enable("false")) multiplexer_28 (
    .in0(multiplexer_12_out), .in1(multiplexer_14_out), .out(four), .sel(shift[1]));
  Multiplexer #(.enable("false")) multiplexer_29 (
    .in0(multiplexer_13_out), .in1(multiplexer_15_out), .out(three), .sel(shift[1]));
  Multiplexer #(.enable("false")) multiplexer_30 (
    .in0(multiplexer_14_out), .in1(multiplexer_16_out), .out(two), .sel(shift[1]));
  Multiplexer #(.enable("false")) multiplexer_31 (.in0(multiplexer_15_out), .in1(1'b0), .out(one), .sel(shift[1]));
  Multiplexer #(.enable("false")) multiplexer_32 (.in0(multiplexer_16_out), .in1(1'b0), .out(zero), .sel(shift[1]));
  Multiplexer #(.enable("false")) multiplexer_33 (.in0(fift), .in1(el), .out(result[0]), .sel(shift[2]));
  Multiplexer #(.enable("false")) multiplexer_34 (.in0(fourt), .in1(ten), .out(result[1]), .sel(shift[2]));
  Multiplexer #(.enable("false")) multiplexer_35 (.in0(thirt), .in1(nine), .out(result[2]), .sel(shift[2]));
  Multiplexer #(.enable("false")) multiplexer_36 (.in0(twelf), .in1(eight), .out(result[3]), .sel(shift[2]));
  Multiplexer #(.enable("false")) multiplexer_37 (.in0(el), .in1(seven), .out(result[4]), .sel(shift[2]));
  Multiplexer #(.enable("false")) multiplexer_38 (.in0(ten), .in1(six), .out(result[5]), .sel(shift[2]));
  Multiplexer #(.enable("false")) multiplexer_39 (.in0(nine), .in1(five), .out(result[6]), .sel(shift[2]));
  Multiplexer #(.enable("false")) multiplexer_40 (.in0(eight), .in1(four), .out(result[7]), .sel(shift[2]));
  Multiplexer #(.enable("false")) multiplexer_41 (.in0(seven), .in1(three), .out(result[8]), .sel(shift[2]));
  Multiplexer #(.enable("false")) multiplexer_42 (.in0(six), .in1(two), .out(result[9]), .sel(shift[2]));
  Multiplexer #(.enable("false")) multiplexer_43 (.in0(five), .in1(one), .out(result[10]), .sel(shift[2]));
  Multiplexer #(.enable("false")) multiplexer_44 (.in0(four), .in1(zero), .out(result[11]), .sel(shift[2]));
  Multiplexer #(.enable("false")) multiplexer_45 (.in0(three), .in1(1'b0), .out(result[12]), .sel(shift[2]));
  Multiplexer #(.enable("false")) multiplexer_46 (.in0(two), .in1(1'b0), .out(result[13]), .sel(shift[2]));
  Multiplexer #(.enable("false")) multiplexer_47 (.in0(one), .in1(1'b0), .out(result[14]), .sel(shift[2]));
  Multiplexer #(.enable("false")) multiplexer_48 (.in0(zero), .in1(1'b0), .out(result[15]), .sel(shift[2]));

  // Other names for the same wires on the sheet: out0 = result[0]; out1 = result[1]; out2 = result[2];
  //   out3 = result[3]; out4 = result[4]; out5 = result[5]; out6 = result[6]; out7 = result[7]; out8 = result[8];
  //   out9 = result[9]; out10 = result[10]; out11 = result[11]; out12 = result[12]; out13 = result[13];
  //   out14 = result[14]; out15 = result[15]

  // Notes on the sheet:
  //   14
  //   10
  //   9
  //   8
  //   7
  //   4
  //   2
  //   1
  //   0
  //   13
  //   12
  //   11
  //   6
  //   5
  //   3
endmodule
